# Fritzing sketch MorseLight_1 (saved by Fritzing 0.9.10b)

parts:
  Mod1 = seeeduino-xiao
  Q1 = Basic FET N-Channel [part_number=RFZ44N package="TO220 [THT]"]
  R1 = Resistor [tolerance=±5% resistance=220 package="0402 [SMD]"]
  LED1 = LED - 3mm [color="Red (633nm)" current=0.030 package="3 mm [THT]"]

nets:
  N1: Mod1.D9, Q1.gate, R1.Pin_0
  N2: Mod1.GND, Q1.source, R1.Pin_1
  N3: Q1.drain, LED1.cathode

notes:
  RFZ44N
  16340 BatteryPack
  <- GND
  <- 3.3v

custom parts:
  seeeduino-xiao: Seeeduino XIAO processor board.
